# Fritzing sketch Схема модема (saved by Fritzing 0.9.10b)

parts:
  Компонент1 = Arduino Nano (Rev3.0)
  RF4 = E07-M11010

nets:
  N1: Компонент1.D9, RF4.3_GDO0
  N2: Компонент1.D10, RF4.4_CSN
  N3: Компонент1.D11/MOSI, RF4.6_MOSI
  N4: Компонент1.D12/MISO, RF4.7_MISO/GDO1
  N5: Компонент1.GND, RF4.1_GND
  N6: Компонент1.3V3, RF4.2_VCC
  N7: Компонент1.D13/SCK, RF4.5_SCK
