# Fritzing sketch Схема робота (saved by Fritzing 0.9.10b)

parts:
  Компонент1 = Arduino Nano (Rev3.0) (ICSP)
  Pololu_A2 = DRV 8825 Stepper Motor Carrier, High Current [part_number="DRV 8825"]
  Pololu_A3 = DRV 8825 Stepper Motor Carrier, High Current [part_number="DRV 8825"]
  JP1 = Header 5x2 [package=2x5-ra]
  RF3 = E07-M11010
  S1 = Momentary Switch [package=ksa_sealed_tac_switch]
  J1 = Piezo Speaker
  J2 = Basic Servo
  HC-SR04_Sensor_1 = HC-SR04 Ultrasonic Distance Sensor
  M1 = Stepper Motor - Bipolar
  M2 = Stepper Motor - Bipolar

nets:
  N1: Компонент1.D2, HC-SR04_Sensor_1.TRIG
  N2: Компонент1.D3, Pololu_A2.DIRECTION
  N3: Компонент1.D4, Pololu_A3.DIRECTION
  N4: Компонент1.D5, HC-SR04_Sensor_1.ECHO
  N5: Компонент1.D6, Pololu_A2.STEP
  N6: Компонент1.D7, Pololu_A3.STEP
  N7: Компонент1.D8, Pololu_A2.ENABLE, Pololu_A3.ENABLE
  N8: Компонент1.D9, JP1.5, RF3.3_GDO0
  N9: Компонент1.D10, JP1.3, RF3.4_CSN
  N10: Компонент1.D11/MOSI, JP1.1, RF3.6_MOSI
  N11: Компонент1.D12/MISO, JP1.8, RF3.7_MISO/GDO1
  N12: Компонент1.A7, JP1.pin_14
  N13: Компонент1.A6, JP1.pin_13
  N14: Компонент1.A3, JP1.pin_12
  N15: Компонент1.A2, JP1.pin_11, J2.pulse
  N16: Компонент1.A1, JP1.10, J1.pin2
  N17: Компонент1.A0, JP1.9, S1.3
  N18: Компонент1.3V3, RF3.2_VCC
  N19: Компонент1.D13/SCK, JP1.7, RF3.5_SCK
  N20: Pololu_A2.OUT_2B, M1.A
  N21: Pololu_A2.OUT_2A, M1.C
  N22: Pololu_A2.OUT_1A, M1.B
  N23: Pololu_A2.OUT_1B, M1.D
  N24: Pololu_A3.OUT_2B, M2.A
  N25: Pololu_A3.OUT_2A, M2.C
  N26: Pololu_A3.OUT_1A, M2.B
  N27: Pololu_A3.OUT_1B, M2.D
  N28: JP1.pin_27, JP1.pin_28
  N29: JP1.pin_29, JP1.pin_30

notes:
  3,3В

custom parts:
  Header 5x2: Header 5x2 Standard 10-pin dual row 0.1 header. Commonly used with AVR-ISP. Use with Spark Fun Electronics SKU: PRT-00778
